# Fritzing sketch GuardTank (saved by Fritzing 0.9.9b)
breadboards: 2

parts:
  M1 = DC Motor
  M2 = DC Motor
  WeMos_D1_Mini1 = WeMos D1 Mini  # not connected
  元件2 = Motor Driver 1A Dual TB6612FNG
  VCC1 = Battery block 9V
  M4 = Dagu DGServo 9g (Top view) [part_number=RS001B]
  M5 = Dagu DGServo 9g (Top view) [part_number=RS001B]
  M6 = RioRand LM2596

nets:
  GND: M1.pin_1, 元件2.GND, VCC1.-, M4.gnd, M5.gnd, M6.Pin_1, M6.Pin_4
  N1: M1.pin_2, 元件2.B01
  N2: M2.pin_1, 元件2.A02
  N3: M2.pin_2, 元件2.A01
  N4: 元件2.VCC, 元件2.STBY, M6.Pin_3
  VCC: 元件2.VM, VCC1.+, M4.vcc, M5.vcc, M6.Pin_2
